# Fritzing sketch laundrybox (saved by Fritzing 1.0.7)

parts:
  Load_cell = Load cell
  HX711 = HX711
  M5Stack_U107 = M5Stack U107
  Raspberry_Pi = Raspberry Pi  # not connected
  Metal_detector = Metal detector
  A1 = Teensy 4.1

nets:
  N1: Load_cell.E+, HX711.E+
  N2: Load_cell.E-, HX711.E-
  N3: Load_cell.A+, HX711.A+
  N4: Load_cell.A-, HX711.A-
  N5: HX711.VCC, A1.Pin_26
  GND: HX711.GND, M5Stack_U107.GND, Metal_detector.GND, A1.Pin_12, A1.Pin_50, A1.Pin_63
  N6: HX711.DT, A1.Pin_15
  N7: HX711.SCK, A1.Pin_16
  N8: M5Stack_U107.5V, A1.Pin_64
  N9: M5Stack_U107.TXD, A1.Pin_13
  N10: Metal_detector.SIG, A1.Pin_52

custom parts:
  Metal detector: Ferrous-metal detector — indicator LED output read on Teensy A0
  Teensy 4.1: The Teensy is a complete USB-based microcontoller development system, in a very small footprint, capable of implementing many types of projects. All programming is done via the USB port. No special programmer is needed, only a standard micro-USB cable and a PC or Macintosh with a USB port.
